// Logisim project D1 - Copy (2).circ as structural Verilog: 1 circuit, main circuit main
module main (
  input  x,
  input  y,
  input  x_2,
  input  y_2,
  input  x_3,
  input  x_4,
  input  y_3,
  input  in_8,
  input  in_9,
  output x_y,
  output x_y_2,
  output nx,
  output x__y,
  output x_y_3
);

  not not_1 (nx, x_3);
  or or_1 (x_y, x, y);
  and and_1 (x_y_2, x_2, y_2);
  xor xor_1 (x__y, x_4, y_3);
  xnor xnor_1 (x_y_3, in_8, in_9);

  // Notes on the sheet:
  //   OR GATE
  //   AND GATE
  //   NOT GATE
  //   XOR GATE
  //   XNOR GATE
endmodule
