// Logisim project D15.circ as structural Verilog: 1 circuit, main circuit main
module main (
  input  j,
  input  k,
  input  D,
  input  T,
  output Q,
  output Q_prime,
  output Q_2,
  output Q_prime_2,
  output Q_3,
  output Q_prime_3
);

  wire clock_1_out, clock_2_out, clock_3_out;

  Clock clock_1 (.out(clock_1_out));
  Clock clock_2 (.out(clock_2_out));
  Clock clock_3 (.out(clock_3_out));
  J_K_Flip_Flop j_k_ff_1 (.J(j), .clk(clock_1_out), .K(k), .Q(Q), .Qn(Q_prime));  // open: preset, en, reset
  // D_Flip_Flop d_ff_1: pin names not known; wires that end beside it: clock_2_out, D, Q_2, Q_prime_2
  T_Flip_Flop t_ff_1 (.T(T), .Q(Q_3), .Qn(Q_prime_3));  // open: clk, preset, reset, en

  // Notes on the sheet:
  //   clk
  //   clk
  //   clk
  //   JK-FLIPELOP
  //   D-FLIPELOP
  //   T-FLIPELOP
endmodule
