// Logisim project D17.circ as structural Verilog: 1 circuit, main circuit main
module main (
  input  in_1
);

  wire and_1_out, clock_1_out, t_ff_1_q, t_ff_2_q, t_ff_3_q;

  Clock clock_1 (.out(clock_1_out));
  T_Flip_Flop t_ff_1 (.clk(clock_1_out), .T(in_1), .Q(t_ff_1_q));  // open: Qn, preset, reset, en
  LED led_1 ();  // open: in
  T_Flip_Flop t_ff_2 (.clk(clock_1_out), .Q(t_ff_2_q));  // open: T, Qn, preset, reset, en
  LED led_2 ();  // open: in
  and and_1 (and_1_out, t_ff_1_q, t_ff_2_q);
  LED led_3 ();  // open: in
  T_Flip_Flop t_ff_3 (.clk(clock_1_out), .T(and_1_out), .Q(t_ff_3_q));  // open: Qn, preset, reset, en
endmodule
