// Logisim project D19.circ as structural Verilog: 1 circuit, main circuit main
module main (
  input  A,
  input  B,
  input  C_in,
  input  [1:0] opeartion,
  output Result,
  output c_out
);

  wire and_1_out, or_1_out, undriven;

  or or_1 (or_1_out, A, B);
  and and_1 (and_1_out, A, B);
  Adder #(.width(1)) adder_1 (.a(A), .b(B), .cout(c_out));  // open: out, cin
  Multiplexer #(.select(2)) multiplexer_1 (
    .in0(or_1_out), .in1(and_1_out), .in2(and_1_out), .in3(undriven), .out(Result), .sel(opeartion));  // open: en
endmodule
