// Logisim project D2 - Copy.circ as structural Verilog: 1 circuit, main circuit main
module main (
  input  X,
  input  Y,
  input  X_2,
  input  Y_2,
  input  X_3,
  output out_6,
  output out_7,
  output out_8
);

  wire nand_1_out, nand_2_out, nand_3_out;

  nand nand_1 (nand_1_out, X, Y);
  nand nand_2 (nand_2_out, X_2, X_2);
  nand nand_3 (nand_3_out, Y_2, Y_2);
  nand nand_4 (out_8, X_3, X_3);
  nand nand_5 (out_6, nand_1_out, nand_1_out);
  nand nand_6 (out_7, nand_2_out, nand_3_out);

  // Notes on the sheet:
  //   '(X.Y)
  //   'X+'Y
  //   'X+'Y
  //   NAND TO AND
  //   'X
  //   'Y
  //   NAND TO OR
  //   'X
  //   NAND TO NOT
  //   X.Y
  //   X+Y
endmodule
