// Logisim project D20.circ as structural Verilog: 1 circuit, main circuit main
module main (
  input  A0,
  input  B0,
  input  A1,
  input  B1,
  input  A2,
  input  B2,
  input  A3,
  input  B3,
  output S0,
  output S1,
  output S2,
  output S3,
  output S4
);

  Adder #(.width(1)) adder_1 (.a(A0), .b(B0), .out(S0));  // open: cin, cout
  Adder #(.width(1)) adder_2 (.a(A1), .b(B1), .out(S1));  // open: cin, cout
  Adder #(.width(1)) adder_3 (.a(A2), .b(B2), .out(S2));  // open: cin, cout
  Adder #(.width(1)) adder_4 (.a(A3), .b(B3), .out(S3), .cout(S4));  // open: cin
endmodule
