// Logisim project D3 - Copy.circ as structural Verilog: 1 circuit, main circuit main
module main (
  input  X,
  input  Y,
  input  X_2,
  input  Y_2,
  input  X_3,
  output out_6,
  output out_7,
  output out_8
);

  wire nor_1_out, nor_2_out, nor_3_out;

  nor nor_1 (nor_1_out, X, Y);
  nor nor_2 (nor_2_out, X_2, X_2);
  nor nor_3 (nor_3_out, Y_2, Y_2);
  nor nor_4 (out_8, X_3, X_3);
  nor nor_5 (out_7, nor_2_out, nor_3_out);
  nor nor_6 (out_6, nor_1_out, nor_1_out);

  // Notes on the sheet:
  //   '(X+Y)
  //   NPR TO NOT
  //   'X.'Y
  //   'X.'Y
  //   NOR TO OR
  //   'X
  //   'Y
  //   NOR TO AND
  //   'X
  //   X+Y
  //   X.Y
endmodule
